# Fritzing sketch BikeUSB (saved by Fritzing 0.9.3b)
circuit board: 4.19683cm x 2.69825cm

parts:
  X1 = USB Connectors [package=usb-a-s-silk-female]
  U1 = Voltage Regulator - 5V [package="TO220 [THT]"]
  SJ1 = Solder Jumper [package=sj_2s]
  J1 = Screw terminal - 2 pins [package=THT]
  D1 = Rectifier Diode [part_number=1N4001 package="300 mil [THT]"]
  D2 = Rectifier Diode [part_number=1N4001 package="300 mil [THT]"]
  D3 = Rectifier Diode [part_number=1N4001 package="300 mil [THT]"]
  D4 = Rectifier Diode [part_number=1N4001 package="300 mil [THT]"]
  C1 = Electrolytic Capacitor [capacitance=999µF voltage=10V package="200 mil [THT, electrolytic]"]
  C2 = Electrolytic Capacitor [capacitance=999µF voltage=10V package="200 mil [THT, electrolytic]"]
  LED2 = LED - 3mm [color="Blue (525nm)" package="3 mm [THT]"]
  LED1 = LED - 3mm [color="Blue (430nm)" package="3 mm [THT]"]
  R1 = Resistor [tolerance=±5% resistance=470 package=THT]
  R2 = Resistor [tolerance=±5% resistance=220 package=THT]

nets:
  N1: X1.D+, SJ1.2
  N2: X1.D-, SJ1.1
  GND: X1.GND, U1.GND, D3.cathode, D4.cathode, C1.-, C2.-, LED2.cathode, LED1.cathode
  N3: X1.VBUS, U1.output_voltage, R2.Pin_1
  N4: U1.input_voltage, D1.cathode, D2.cathode, C1.+, C2.+, R1.Pin_1
  N5: J1.pin1, D2.anode, D4.anode
  N6: J1.pin2, D1.anode, D3.anode
  N7: LED2.anode, R2.Pin_0
  N8: LED1.anode, R1.Pin_0
